# Fritzing sketch Polysix OTA Overdrive Enabler (saved by Fritzing 0.9.2b)
circuit board: 7.77019cm x 3.61958cm
breadboards: 1

parts:
  U2 = LM13600 [package="DIP16 [THT]"]
  J2 = female pin header, 1 pin [form="♀ (female)"]
  J3 = female pin header, 1 pin [form="♀ (female)"]
  J4 = female pin header, 1 pin [form="♀ (female)"]
  J5 = female pin header, 1 pin [form="♀ (female)"]
  J7 = female pin header, 3 pins [form="♀ (female)"]
  J12 = female pin header, 1 pin [form="♀ (female)"]
  J13 = female pin header, 1 pin [form="♀ (female)"]
  J14 = female pin header, 1 pin [form="♀ (female)"]
  J15 = female pin header, 1 pin [form="♀ (female)"]
  J10 = female pin header, 3 pins [form="♀ (female)"]
  J6 = female pin header, 3 pins [form="♀ (female)"]
  U3 = LM13600 [package="DIP16 [THT]"]
  J11 = female pin header, 3 pins [form="♀ (female)"]
  U1 = AD5262 [part_number=AD5262 package=tssop16]
  XTAL1 = Crystal [frequency="16 Mhz" package=THT]
  C1 = Ceramic Capacitor [capacitance=22pF voltage=10V package="200 mil [THT, multilayer]"]
  C2 = Ceramic Capacitor [capacitance=22pF voltage=10V package="200 mil [THT, multilayer]"]
  R1 = Resistor [tolerance=±5% resistance=10k package=THT]
  R2 = Resistor [tolerance=±5% resistance=1k package=THT]
  R3 = Resistor [tolerance=±5% resistance=1k package=THT]
  J32 = female pin header, 6 pins [form="♀ (female)"]
  J34 = AVR ISP 6 Pin [package=2x3-ns]
  J9 = female pin header, 3 pins [form="♀ (female)"]
  C6 = Ceramic Capacitor [capacitance=100nF package="100 mil [THT, multilayer]"]
  C4 = Ceramic Capacitor [capacitance=100nF voltage=10V package="100 mil [THT, multilayer]"]
  C3 = Ceramic Capacitor [capacitance=100nF voltage=10V package="100 mil [THT, multilayer]"]
  C5 = Electrolytic Capacitor [capacitance=10µF voltage=10V package="100 mil [THT, electrolytic]"]
  J35 = double row female pin header, 12 pins [form="♀ (female)"]
  J37 = female pin header, 5 pins [form="♀ (female)"]  # not connected
  Atmega328 = ATmega328 [package=tqfp]
  J36 = female pin header, 7 pins [form="♀ (female)"]  # not connected
  J38 = female pin header, 1 pin [form="♀ (female)"]

nets:
  N1: U2.AmpBiasA, J2.pin1
  N2: U2.DiodeBiasA, U3.DiodeBiasA
  N3: U2.InA+, U3.InA+
  N4: U2.InA-, J12.pin1
  N5: U2.OutA, U3.OutA
  N6: U2.V-, U3.V-
  N7: U2.BuffInA, U3.BuffInA
  N8: U2.BuffOutA, U3.BuffOutA
  N9: U2.BuffOutB, U3.BuffOutB
  N10: U2.BuffInB, U3.BuffInB
  N11: U2.V+, U3.V+
  N12: U2.OutB, U3.OutB
  N13: U2.InB-, J14.pin1
  N14: U2.InB+, U3.InB+
  N15: U2.DiodeBiasB, U3.DiodeBiasB
  N16: U2.AmpBiasB, J4.pin1
  N17: J3.pin1, U3.AmpBiasA
  N18: J5.pin1, U3.AmpBiasB
  N19: J7.pin1, J11.pin1, U1.A2
  N20: J7.pin2, J11.pin2, U1.W2
  N21: J7.pin3, J11.pin3, U1.B2
  N22: J13.pin1, U3.InA-
  N23: J15.pin1, U3.InB-
  N24: J10.pin1, J6.pin1, U1.A1
  N25: J10.pin2, J6.pin2, U1.W1
  N26: J10.pin3, J6.pin3, U1.B1
  5V: U1.VDD, U1._SHDN, U1._PR, U1.VL, R1.Pin_0, J32.pin3, J34.2, J9.pin1, C6.1, C5.+, J35.pin8, Atmega328.VCC, Atmega328.AVCC
  SCK: U1.CLK, J34.3, Atmega328.PB5(SCK)
  MOSI: U1.SDI, J34.4, Atmega328.PB3(MOSI_OC2)
  D10: U1._CS, Atmega328.PB2(SS_OC1B), J38.pin1
  GND: U1.GND, C1.0, C2.0, J32.pin1, J32.pin2, J34.6, J9.pin2, C6.0, C3.0, C5.-, J35.pin7, Atmega328.GND, Atmega328.AGND
  -5V: U1.VSS, J9.pin3
  N27: XTAL1.pin_0, C2.1, Atmega328.PB7(XTAL2_TOSC2)
  N28: XTAL1.pin_1, C1.1, Atmega328.PB6(XTAL1_TOSC1)
  RESET: R1.Pin_1, J34.5, C4.1, Atmega328.PC6(_RESET)
  N29: R2.Pin_0, Atmega328.PD0(RXD)
  RXD: R2.Pin_1, J32.pin4
  N30: R3.Pin_0, Atmega328.PD1(TXD)
  TXD: R3.Pin_1, J32.pin5
  DTR: J32.pin6, C4.0
  MISO: J34.1, Atmega328.PB4(MISO)
  N31: C3.1, Atmega328.AREF
  A5: J35.pin1, Atmega328.PC5(ADC5_SCL)
  A4: J35.pin2, Atmega328.PC4(ADC4_SDA)
  A3: J35.pin3, Atmega328.PC3(ADC3)
  A2: J35.pin4, Atmega328.PC2(ADC2)
  A1: J35.pin5, Atmega328.PC1(ADC1)
  A0: J35.pin6, Atmega328.PC0(ADC0)
  D5: J35.pin9, Atmega328.PD5(T1)
  D4: J35.pin10, Atmega328.PD4(XCK_T0)
  D3: J35.pin11, Atmega328.PD3(INT1)
  D2: J35.pin12, Atmega328.PD2(INT0)

notes:
  W1
  GND
  Polysix Drive
  Dec 2015
  InB-
  (U2)
  (U3)
  InA-
  A1
  synthhacker.blogspot.com
  B1
  AmpA
  AmpB
  +5V
  -5V
  LM13600
  Gnd
  CTS
  TXO
  RXI
  DTR
  D2
  D3
  D4
  A3
  A5
  A0
  A2
  A4
  MISO
  SCK
  RESET
  MOSI
  B2
  W2
  AD
  5262
  D5
  D10
  FTDI Serial Header
  Arduino Pins
  Arduino Uno Compatible
  ICSP Header
  Spare Holes
  Power Filtering
  Power
  Dual Digipot (SPI)
  Pot 1 Header
  Pot 2 Header
  DIP Socket
  DIP Connector

custom parts:
  LM13600: Dual Operational Transconductance Amplifiers with Linearizing Diodes and Buffers. +/- 15V
  AD5262: Digital Potentiometer, 20K, 2-Channel, 256-step
